# Fritzing sketch WagonControl (saved by Fritzing 0.9.3b)

parts:
  Part1 = Arduino Nano (Rev3.0) (ICSP)
  Vcc(5V) = Header 11 [package=1x11_smd_no_holes]
  GND = Header 11 [package=1x11_smd_no_holes]
  hc-sr1 = hc-sr04
  BT1 = Bluetooth HC-06u [package=THT]
  Part3 = Black Joystick KY-023
  Motor-R = Header 2 [package=springterminal-2.54mm-2]
  Motor-L = Header 2 [package=springterminal-2.54mm-2]
  S1 = H-Bridge with L298N
  M1 = DC Motor

nets:
  N1: Part1.D2, hc-sr1.Echo
  N2: Part1.D3, S1.IN2
  N3: Part1.D4, BT1.TXD
  N4: Part1.D5, BT1.RXD
  N5: Part1.D6, S1.IN1
  N6: Part1.D7, hc-sr1.Trig
  N7: Part1.D9, Motor-R.2
  N8: Part1.D10, Motor-L.2
  N9: Part1.D11/MOSI, Motor-R.1
  N10: Part1.D12/MISO, Motor-L.1
  N11: Part1.GND, GND.6
  N12: Part1.5V, Vcc(5V).1
  N13: Part1.A1, Part3.VRx
  N14: Part1.A0, Part3.VRy
  N15: Vcc(5V).2, Part3.+5V
  N16: Vcc(5V).5, BT1.VCC
  N17: Vcc(5V).11, hc-sr1.VCC
  N18: GND.1, Part3.GND
  N19: GND.8, BT1.GND
  N20: GND.9, S1.GND
  N21: GND.11, hc-sr1.GND
  N22: S1.ENA, S1.ENA-5V
  N23: S1.M1-01, M1.pin_2
  N24: S1.M1-02, M1.pin_1

notes:
  12V
  Do not connect the 5V!!!
  Or connect it instead of the input connection from the motor driver.

custom parts:
  Bluetooth HC-06u: Bluetooth HC-06 - face up, pins down 16.5mm x 37.5mm PCB
  Black Joystick KY-023: Description: The joystick is a combination of 2 analoog potentiometer and a digital switch. Arduino GND --> Module pin - Arduino +5V --> Module pin +5V Arduino Analoog 0 --> Module VRx Arduino Analoog 1 --> Module VRy Arduino Digital --> Module SW Dimensions: 1" x 1.25"
  H-Bridge with L298N: h-bridge
